# Fritzing sketch ultrasonic-sensor (saved by Fritzing 0.9.2b)
breadboards: 1

parts:
  Parte1 = Arduino Uno (Rev3)
  SONAR1 = Maxbotix MaxSonar Ultrasonic Sensor (Hi-Res)

nets:
  N1: Parte1.D7, SONAR1.PW
  5V: Parte1.5V, SONAR1.+5V
  GND: Parte1.GND, SONAR1.GND

custom parts:
  Maxbotix MaxSonar Ultrasonic Sensor (Hi-Res): Maxbotix MaxSonar Hi-Resolution Ultrasonic Sensor HRLV-EZ0, HRLV-EZ1, HRLV-EZ2, HRLV-EZ3, HRLV-EZ4
